# Fritzing sketch projeto_A4 (saved by Fritzing 0.9.5d)

parts:
  U1 = NodeMCU V3.0
  YF-S201_Flow_Meter2 = YF-S201 Water Flow Meter
  LED2 = LED - 5mm [color="Red (633nm)" package="5 mm [THT]"]
  R1 = Resistor [tolerance=±5% resistance=220 package=THT]  # not connected

nets:
  N1: U1.D2, YF-S201_Flow_Meter2.SIG
  GND: U1.GND, YF-S201_Flow_Meter2.GND, LED2.cathode
  3V3: U1.3V3, YF-S201_Flow_Meter2.VCC

custom parts:
  NodeMCU V3.0: ESP8266 based NodeMCU
  YF-S201 Water Flow Meter: The YF-S201 Flow Meter. The input voltage is 5V to 24V (DC).

// code stored in the sketch: projeto_A4.ino
#include <ESP8266WiFi.h>
#include <PubSubClient.h>

// Credenciais Wi-Fi
const char* ssid = "SEU_SSID";
const char* password = "SUA_SENHA";

// Broker MQTT
const char* mqtt_server = "broker.hivemq.com"; // Pode usar outro se quiser

WiFiClient espClient;
PubSubClient client(espClient);

// Sensor e atuador
const int PINO_SENSOR = D2;
const int PINO_LED = D1;
volatile unsigned long contador = 0;

const float FATOR_CALIBRACAO = 4.5;
unsigned long tempo_antes = 0;
float fluxo = 0;
float volume_total = 0;

void contador_pulso() {
  contador++;
}

void setup_wifi() {
  WiFi.begin(ssid, password);
  while (WiFi.status() != WL_CONNECTED) {
    delay(500);
  }
}

void reconnect() {
  while (!client.connected()) {
    client.connect("ESP8266Client");
  }
}

void setup() {
  Serial.begin(9600);
  pinMode(PINO_SENSOR, INPUT_PULLUP);
  pinMode(PINO_LED, OUTPUT);
  
  attachInterrupt(digitalPinToInterrupt(PINO_SENSOR), contador_pulso, FALLING);

  setup_wifi();
  client.setServer(mqtt_server, 1883);
  tempo_antes = millis();
}

void loop() {
  if (!client.connected()) {
    reconnect();
  }
  client.loop();

  if (millis() - tempo_antes > 1000) {
    detachInterrupt(digitalPinToInterrupt(PINO_SENSOR));

    fluxo = ((1000.0 / (millis() - tempo_antes)) * contador) / FATOR_CALIBRACAO;
    float volume = fluxo / 60.0;
    volume_total += volume;

    // Atuador: liga LED se fluxo > 1.0 L/min
    if (fluxo > 1.0) {
      digitalWrite(PINO_LED, HIGH);
    } else {
      digitalWrite(PINO_LED, LOW);
    }

    // Envio MQTT
    char fluxoMsg[32];
    dtostrf(fluxo, 6, 2, fluxoMsg);
    client.publish("agua/fluxo", fluxoMsg);

    char volumeMsg[32];
    dtostrf(volume_total, 6, 2, volumeMsg);
    client.publish("agua/volume", volumeMsg);

    Serial.print("Fluxo: "); Serial.print(fluxo); Serial.println(" L/min");
    Serial.print("Volume Total: "); Serial.println(volume_total);

    contador = 0;
    tempo_antes = millis();
    attachInterrupt(digitalPinToInterrupt(PINO_SENSOR), contador_pulso, FALLING);
  }
}
